# Fritzing sketch fuszerkert (saved by Fritzing 0.9.3b)
breadboards: 2

parts:
  Part1 = Arduino Uno (Rev3)
  Part2 = SRF05 Ultrasonic Rangefinder
  Part3 = FC-28 Soil Hygrometer Module - Probe
  Part4 = FC-28 Soil Hygrometer Module
  R1 = PHOTOCELL [package=photocell-kit]
  R2 = Resistor [tolerance=±5% resistance=10k package="0805 [SMD]"]
  Power_plug1 = Power plug
  KY-1 = Keyes Relay [package=THT]
  KY-2 = Keyes Relay [package=THT]
  KY-3 = Keyes Relay [package=THT]
  Part5 = FC-28 Soil Hygrometer Module - Probe
  Part6 = FC-28 Soil Hygrometer Module
  Part7 = FC-28 Soil Hygrometer Module - Probe
  Part8 = FC-28 Soil Hygrometer Module
  LED2 = LED - 5mm [color="Green (570nm)" package="5 mm [THT]"]
  LED3 = LED - 5mm [color="Red (633nm)" package="5 mm [THT]"]
  LED_STRIP = smd LED [color="White (4500K)" package="0805 [SMD]"]
  M1 = DC Motor
  J1 = Piezo Speaker
  LED1 = RGB LED (com. cathode, rbg) [package="5 mm [THT]"]
  R3 = Resistor [tolerance=±5% resistance=220 package="0402 [SMD]"]
  R4 = Resistor [tolerance=±5% resistance=220 package="0402 [SMD]"]
  R5 = Resistor [tolerance=±5% resistance=220 package="0402 [SMD]"]
  R6 = Resistor [tolerance=±5% resistance=220 package="0402 [SMD]"]  # not connected
  R7 = Resistor [tolerance=±5% resistance=220 package="0402 [SMD]"]

nets:
  N1: Part1.A0, R1.P$2, R2.Pin_1
  N2: Part1.A1, Part8.AO
  N3: Part1.A2, Part6.AO
  N4: Part1.A3, Part4.AO
  N5: Part1.D8, KY-3.signal
  N6: Part1.D9_PWM, Part2.Trig
  N7: Part1.D10_PWM/SS, Part2.Echo
  N8: Part1.D11_PWM/MOSI, J1.pin2
  N9: Part1.D2, R3.Pin_1
  N10: Part1.D3_PWM, R4.Pin_1
  N11: Part1.D4, R5.Pin_1
  N12: Part1.D5_PWM, R7.Pin_1
  N13: Part1.D6_PWM, KY-2.signal
  N14: Part1.D7, KY-1.signal
  5V: Part1.5V, Part2.VCC, R1.P$1, KY-1.power, KY-1.NO, KY-2.power, KY-3.power
  GND: Part2.GND, Part4.GND, R2.Pin_0, Power_plug1.GND, KY-1.ground, KY-2.ground, KY-3.ground, Part6.GND, Part8.GND, LED2.cathode, LED3.cathode, LED_STRIP.cathode, M1.pin_2, J1.pin1, LED1.common_cathode
  N15: Part3.POS, Part4.POS
  N16: Part3.NEG, Part4.NEG
  VCC: Part4.VCC, KY-1.C, Part6.VCC, Part8.VCC
  N17: Power_plug1.VCC, KY-2.NO, KY-3.NO
  N18: KY-2.C, M1.pin_1
  N19: KY-3.C, LED_STRIP.anode
  N20: Part5.POS, Part6.POS
  N21: Part5.NEG, Part6.NEG
  N22: Part7.POS, Part8.POS
  N23: Part7.NEG, Part8.NEG

custom parts:
  FC-28 Soil Hygrometer Module - Probe: The FC-28 is a soil hygrometer module that uses the Texas Instruments LM393 comparator chip to provide an analog measurement of soil humidity.
  FC-28 Soil Hygrometer Module: The FC-28 is a soil hygrometer module that uses the Texas Instruments LM393 comparator chip to provide an analog measurement of soil humidity. The digital output is high when soil moisture is over a certain threshold, as determined by adjusting the potentiometer.
  Keyes Relay: The Keyes 5V relay module is suitable for SCM development, home appliance control. It uses a 5V~12V TIL control signal which can control DC / AC signal.
